// Logisim project ARM_CPU.circ as structural Verilog: 14 circuits, main circuit main
module main (
  input  [1:0] Program_num,
  input  CLR
);

  wire CLK_out, comparator_1_eq, control_unit_1_alusrc, control_unit_1_bl, control_unit_1_bx,
       control_unit_1_mem2reg, control_unit_1_memwrite, control_unit_1_mov, control_unit_1_pcsrc,
       control_unit_1_regwrite;
  wire [1:0] control_unit_1_alucontrol1_0, control_unit_1_immsrc1_0, control_unit_1_regsrc1_0;
  wire [3:0] alu_1_alu_flags, multiplexer_2_out, multiplexer_3_out, multiplexer_4_out;
  wire [7:0] adder_1_out, adder_2_out, multiplexer_1_out, PC_q;
  wire [31:0] alu_1_result, bit_extender_1_out, data_memory_1_rd, extend_1_imm, instruction_memory_1_iw, LR,
       multiplexer_5_out, multiplexer_6_out, n16_register_file_1_rd1, n16_register_file_1_rd2, PC, R0, R1,
       R2, R3, R4, R5, R6, R7, R8, R9, R10, R11, R12, SP;

  Multiplexer #(.width(8), .enable("false")) multiplexer_1 (
    .in0(adder_1_out), .in1(multiplexer_6_out[7:0]), .out(multiplexer_1_out), .sel(control_unit_1_pcsrc));
  Clock CLK (.out(CLK_out));
  Register u_PC (.D(multiplexer_1_out), .Q(PC_q), .clk(CLK_out), .clr(CLR));  // open: en
  Adder adder_1 (.a(PC_q), .b(8'h4), .out(adder_1_out));  // open: cin, cout
  // Probe on R0
  // Probe on R1
  // Probe on R2
  // Probe on R3
  // Probe on instruction_memory_1_iw
  Instruction_Memory instruction_memory_1 (.Program_Number(Program_num), .A(PC_q), .IW(instruction_memory_1_iw));
  Adder adder_2 (.a(adder_1_out), .b(8'h4), .out(adder_2_out));  // open: cin, cout
  // Probe on R4
  // Probe on R5
  // Probe on R6
  // Probe on R7
  assign bit_extender_1_out = {{24{1'b0}}, adder_2_out};  // Bit_Extender bit_extender_1
  Comparator #(.width(32)) comparator_1 (
    .a(instruction_memory_1_iw), .b(32'heafffffe), .eq(comparator_1_eq));  // open: gt, lt
  Control_Unit control_unit_1 (
    .Cond3_0(instruction_memory_1_iw[31:28]), .ALUFlags3_0(alu_1_alu_flags),
    .Op1_0(instruction_memory_1_iw[27:26]), .Funct5_0(instruction_memory_1_iw[25:20]),
    .Rd(instruction_memory_1_iw[15:12]), .PCSrc(control_unit_1_pcsrc), .RegWrite(control_unit_1_regwrite),
    .MemWrite(control_unit_1_memwrite), .Mem2Reg(control_unit_1_mem2reg), .ALUSrc(control_unit_1_alusrc),
    .ImmSrc1_0(control_unit_1_immsrc1_0), .RegSrc1_0(control_unit_1_regsrc1_0),
    .ALUControl1_0(control_unit_1_alucontrol1_0), .CLK(CLK_out), .Mov(control_unit_1_mov),
    .BL(control_unit_1_bl), .IW(instruction_memory_1_iw), .BX(control_unit_1_bx));
  LED Complete (.in(comparator_1_eq));
  // Probe on R8
  // Probe on R9
  // Probe on R10
  // Probe on R11
  Multiplexer #(.width(4), .enable("false")) multiplexer_2 (
    .in0(instruction_memory_1_iw[19:16]), .in1(4'b1111), .out(multiplexer_2_out),
    .sel(control_unit_1_regsrc1_0[0]));
  Multiplexer #(.width(4), .enable("false")) multiplexer_3 (
    .in0(instruction_memory_1_iw[3:0]), .in1(instruction_memory_1_iw[15:12]), .out(multiplexer_3_out),
    .sel(control_unit_1_regsrc1_0[1]));
  // Probe on R12
  // Probe on SP
  // Probe on LR
  // Probe on PC
  Multiplexer #(.width(4), .enable("false")) multiplexer_4 (
    .in0(instruction_memory_1_iw[15:12]), .in1(4'b1111), .out(multiplexer_4_out), .sel(control_unit_1_bx));
  _16_register_file u_16_register_file_1 (
    .A3(multiplexer_4_out), .WD3(multiplexer_6_out), .CLR(CLR), .A1(multiplexer_2_out),
    .A2(multiplexer_3_out), .RD1(n16_register_file_1_rd1), .RD2(n16_register_file_1_rd2),
    .WE3(control_unit_1_regwrite), .CLK(CLK_out), .R15(bit_extender_1_out), .R15_2(PC), .R14(LR), .R13(SP),
    .R12(R12), .R11(R11), .R10(R10), .R9(R9), .R8(R8), .R7(R7), .R6(R6), .R5(R5), .R4(R4), .R3(R3), .R2(R2),
    .R1(R1), .R0(R0), .BL(control_unit_1_bl));
  Extend extend_1 (.Input(instruction_memory_1_iw[23:0]), .Imm(extend_1_imm), .ImmSrc(control_unit_1_immsrc1_0));
  Multiplexer #(.width(32), .enable("false")) multiplexer_5 (
    .in0(n16_register_file_1_rd2), .in1(extend_1_imm), .out(multiplexer_5_out), .sel(control_unit_1_alusrc));
  ALU alu_1 (
    .ALU_Control(control_unit_1_alucontrol1_0), .A(n16_register_file_1_rd1), .B(multiplexer_5_out),
    .Result(alu_1_result), .ALU_Flags(alu_1_alu_flags), .Mov(control_unit_1_mov));
  Data_Memory data_memory_1 (
    .CLK(CLK_out), .WE(control_unit_1_memwrite), .A(alu_1_result), .WD(n16_register_file_1_rd2),
    .RD(data_memory_1_rd));
  Multiplexer #(.width(32), .enable("false")) multiplexer_6 (
    .in0(alu_1_result), .in1(data_memory_1_rd), .out(multiplexer_6_out), .sel(control_unit_1_mem2reg));
endmodule

module _16_register_file (
  input  CLK,
  input  WE3,
  input  [3:0] A3,
  input  [31:0] WD3,
  input  CLR,
  input  [3:0] A1,
  input  [31:0] R15,
  input  [3:0] A2,
  input  BL,
  output [31:0] RD1,
  output [31:0] RD2,
  output [31:0] R15_2,
  output [31:0] R7,
  output [31:0] R14,
  output [31:0] R6,
  output [31:0] R13,
  output [31:0] R5,
  output [31:0] R12,
  output [31:0] R4,
  output [31:0] R11,
  output [31:0] R3,
  output [31:0] R10,
  output [31:0] R2,
  output [31:0] R9,
  output [31:0] R1,
  output [31:0] R8,
  output [31:0] R0
);

  wire decoder_1_out0, decoder_1_out1, decoder_1_out2, decoder_1_out3, decoder_1_out4, decoder_1_out5,
       decoder_1_out6, decoder_1_out7, decoder_1_out8, decoder_1_out9, decoder_1_out10, decoder_1_out11,
       decoder_1_out12, decoder_1_out13, decoder_1_out14, decoder_1_out15, or_1_out;
  wire [31:0] multiplexer_1_out, subtractor_1_out;

  Decoder_part #(.select(4), .disabled(0)) decoder_1 (
    .out0(decoder_1_out0), .out1(decoder_1_out1), .out2(decoder_1_out2), .out3(decoder_1_out3),
    .out4(decoder_1_out4), .out5(decoder_1_out5), .out6(decoder_1_out6), .out7(decoder_1_out7),
    .out8(decoder_1_out8), .out9(decoder_1_out9), .out10(decoder_1_out10), .out11(decoder_1_out11),
    .out12(decoder_1_out12), .out13(decoder_1_out13), .out14(decoder_1_out14), .out15(decoder_1_out15),
    .sel(A3), .en(WE3));
  or or_1 (or_1_out, decoder_1_out14, BL);
  Multiplexer #(.width(32), .enable("false")) multiplexer_1 (
    .in0(WD3), .in1(subtractor_1_out), .out(multiplexer_1_out), .sel(BL));
  Subtractor #(.width(32)) subtractor_1 (.a(R15), .b(32'h4), .out(subtractor_1_out));  // open: bin, bout
  Register #(.width(32)) register_1 (.D(WD3), .en(decoder_1_out0), .Q(R0), .clk(CLK), .clr(CLR));
  Register #(.width(32)) register_2 (.D(WD3), .en(decoder_1_out1), .Q(R1), .clk(CLK), .clr(CLR));
  Register #(.width(32)) register_3 (.D(WD3), .en(decoder_1_out2), .Q(R2), .clk(CLK), .clr(CLR));
  Register #(.width(32)) register_4 (.D(WD3), .en(decoder_1_out3), .Q(R3), .clk(CLK), .clr(CLR));
  Register #(.width(32)) register_5 (.D(WD3), .en(decoder_1_out4), .Q(R4), .clk(CLK), .clr(CLR));
  Register #(.width(32)) register_6 (.D(WD3), .en(decoder_1_out5), .Q(R5), .clk(CLK), .clr(CLR));
  Register #(.width(32)) register_7 (.D(WD3), .en(decoder_1_out6), .Q(R6), .clk(CLK), .clr(CLR));
  Register #(.width(32)) register_8 (.D(WD3), .en(decoder_1_out7), .Q(R7), .clk(CLK), .clr(CLR));
  Register #(.width(32)) register_9 (.D(WD3), .en(decoder_1_out8), .Q(R8), .clk(CLK), .clr(CLR));
  Register #(.width(32)) register_10 (.D(WD3), .en(decoder_1_out9), .Q(R9), .clk(CLK), .clr(CLR));
  Register #(.width(32)) register_11 (.D(WD3), .en(decoder_1_out10), .Q(R10), .clk(CLK), .clr(CLR));
  Register #(.width(32)) register_12 (.D(WD3), .en(decoder_1_out11), .Q(R11), .clk(CLK), .clr(CLR));
  Register #(.width(32)) register_13 (.D(WD3), .en(decoder_1_out12), .Q(R12), .clk(CLK), .clr(CLR));
  Register #(.width(32)) register_14 (.D(WD3), .en(decoder_1_out13), .Q(R13), .clk(CLK), .clr(CLR));
  Register #(.width(32)) register_15 (.D(multiplexer_1_out), .en(or_1_out), .Q(R14), .clk(CLK), .clr(CLR));
  Multiplexer #(.select(4), .width(32), .enable("false")) multiplexer_2 (
    .in0(R0), .in1(R1), .in2(R2), .in3(R3), .in4(R4), .in5(R5), .in6(R6), .in7(R7), .in8(R8), .in9(R9),
    .in10(R10), .in11(R11), .in12(R12), .in13(R13), .in14(R14), .in15(R15), .out(RD1), .sel(A1));
  Multiplexer #(.select(4), .width(32), .enable("false")) multiplexer_3 (
    .in0(R0), .in1(R1), .in2(R2), .in3(R3), .in4(R4), .in5(R5), .in6(R6), .in7(R7), .in8(R8), .in9(R9),
    .in10(R10), .in11(R11), .in12(R12), .in13(R13), .in14(R14), .in15(R15), .out(RD2), .sel(A2));

  assign R15_2 = R15;
endmodule

module ALU (
  input  [1:0] ALU_Control,
  input  [31:0] A,
  input  [31:0] B,
  input  Mov,
  output [3:0] ALU_Flags,
  output [31:0] Result
);

  wire adder_1_cout, not_2_out, not_3_out, xor_1_out, xor_2_out;
  wire [30:0] multiplexer_2_out;
  wire [31:0] adder_1_out, and_1_out, multiplexer_1_out, not_1_out, or_1_out;

  assign not_1_out = ~B;  // NOT_Gate not_1, 32 bits wide
  Multiplexer #(.width(32), .enable("false")) multiplexer_1 (
    .in0(B), .in1(not_1_out), .out(multiplexer_1_out), .sel(ALU_Control[0]));
  Adder #(.width(32)) adder_1 (
    .a(multiplexer_1_out), .b(A), .out(adder_1_out), .cin(ALU_Control[0]), .cout(adder_1_cout));
  Multiplexer #(.select(2), .width(32), .enable("false")) multiplexer_2 (
    .in0(adder_1_out), .in1(adder_1_out), .in2(and_1_out), .in3(or_1_out),
    .out({ALU_Flags[0], multiplexer_2_out}), .sel(ALU_Control));
  Multiplexer #(.width(32), .enable("false")) multiplexer_3 (
    .in0({ALU_Flags[0], multiplexer_2_out}), .in1(B), .out(Result), .sel(Mov));
  // Probe on A
  assign or_1_out = A | B;  // OR_Gate or_1, 32 bits wide
  assign and_1_out = A & B;  // AND_Gate and_1, 32 bits wide
  // Probe on B
  Comparator #(.width(32)) comparator_1 (
    .a({ALU_Flags[0], multiplexer_2_out}), .b({32{1'b0}}), .eq(ALU_Flags[2]));  // open: gt, lt
  not not_2 (not_2_out, ALU_Control[1]);
  and and_2 (ALU_Flags[1], adder_1_cout, not_2_out);
  xor xor_1 (xor_1_out, A[31], ALU_Flags[0]);
  and and_3 (ALU_Flags[3], not_2_out, xor_1_out, not_3_out);
  ExactlyOne xor_2 (.out(xor_2_out), .in0(ALU_Control[0]), .in1(B[31]), .in2(A[31]));
  not not_3 (not_3_out, xor_2_out);
endmodule

module Data_Memory (
  input  CLK,
  input  WE,
  input  [31:0] A,
  input  [31:0] WD,
  output [31:0] RD
);

  wire not_1_out;
  wire [31:0] shifter_1_out;

  Shifter #(.width(32), .shift("lr")) shifter_1 (.in(A), .\dist (5'b00010), .out(shifter_1_out));
  not not_1 (not_1_out, WE);
  RAM #(.dataWidth(32), .bus("separate")) ram_1 (
    .addr(shifter_1_out[7:0]), .din(WD), .data(RD), .str(WE), .clk(CLK), .ld(not_1_out));  // open: sel, clr
endmodule

module Extend (
  input  [1:0] ImmSrc,
  input  [23:0] Input,
  output [31:0] Imm
);

  wire [23:0] shifter_1_out;
  wire [31:0] bit_extender_1_out, bit_extender_2_out, bit_extender_3_out;

  Shifter #(.width(24)) shifter_1 (.in(Input), .\dist (5'b00010), .out(shifter_1_out));
  assign bit_extender_1_out = {{24{1'b0}}, Input[7:0]};  // Bit_Extender bit_extender_1
  assign bit_extender_2_out = {{20{1'b0}}, Input[11:0]};  // Bit_Extender bit_extender_2
  assign bit_extender_3_out = {{8{shifter_1_out[23]}}, shifter_1_out};  // Bit_Extender bit_extender_3
  Multiplexer #(.select(2), .width(32), .enable("false")) multiplexer_1 (
    .in0(bit_extender_1_out), .in1(bit_extender_2_out), .in2(bit_extender_3_out), .out(Imm), .sel(ImmSrc));  // open: in3
endmodule

module Control_Unit (
  input  CLK,
  input  [3:0] Cond3_0,
  input  [3:0] ALUFlags3_0,
  input  [1:0] Op1_0,
  input  [5:0] Funct5_0,
  input  [3:0] Rd,
  input  [31:0] IW,
  output PCSrc,
  output RegWrite,
  output MemWrite,
  output Mem2Reg,
  output ALUSrc,
  output [1:0] ImmSrc1_0,
  output [1:0] RegSrc1_0,
  output [1:0] ALUControl1_0,
  output BL,
  output Mov,
  output BX
);

  wire decoder_1_memw, decoder_1_mov, decoder_1_nowrite, decoder_1_pcsrc, decoder_1_regw;
  wire [1:0] decoder_1_flagw1_0;

  Decoder decoder_1 (
    .Rd(Rd), .Op(Op1_0), .Funct(Funct5_0), .PCSrc(decoder_1_pcsrc), .Mem2Reg(Mem2Reg), .MemW(decoder_1_memw),
    .ALUSrc(ALUSrc), .ImmSrc1_0(ImmSrc1_0), .RegW(decoder_1_regw), .RegSrc1_0(RegSrc1_0),
    .ALU_Ctl1_0(ALUControl1_0), .FlagW1_0(decoder_1_flagw1_0), .NoWrite(decoder_1_nowrite),
    .Mov(decoder_1_mov), .BL(BL));
  is_branch_exchange is_branch_exchange_1 (.IW(IW), .BX(BX));
  Conditional_Logic conditional_logic_1 (
    .PCS(decoder_1_pcsrc), .RegW(decoder_1_regw), .MemW(decoder_1_memw), .FlagW(decoder_1_flagw1_0),
    .Cond3_0(Cond3_0), .CLK(CLK), .ALUFlags3_0(ALUFlags3_0), .PCSrc(PCSrc), .RegWrite(RegWrite),
    .MemWrite(MemWrite), .NoWrite(decoder_1_nowrite));  // open: CLR
  or or_1 (Mov, decoder_1_mov, BX);
endmodule

module Decoder (
  input  [3:0] Rd,
  input  [1:0] Op,
  input  [5:0] Funct,
  output PCSrc,
  output BL,
  output Mem2Reg,
  output MemW,
  output ALUSrc,
  output [1:0] ImmSrc1_0,
  output RegW,
  output [1:0] RegSrc1_0,
  output [1:0] ALU_Ctl1_0,
  output [1:0] FlagW1_0,
  output NoWrite,
  output Mov
);

  wire main_decoder_1_alu_op, main_decoder_1_branch;

  Main_Decoder main_decoder_1 (
    .Branch(main_decoder_1_branch), .Mem2Reg(Mem2Reg), .MemWrite(MemW), .ALUSrc(ALUSrc),
    .ImmSrc1(ImmSrc1_0[1]), .ImmSrc0(ImmSrc1_0[0]), .RegWrite(RegW), .RegSrc1(RegSrc1_0[1]),
    .RegSrc0(RegSrc1_0[0]), .ALU_op(main_decoder_1_alu_op), .Op1(Op[1]), .Op0(Op[0]), .F5(Funct[5]),
    .F0(Funct[0]), .F4(Funct[4]), .BL(BL));
  PC_Logic pc_logic_1 (.Rd(Rd), .PCS(PCSrc), .RegW(RegW), .Branch(main_decoder_1_branch));
  ALU_Decoder alu_decoder_1 (
    .ALU_Ctl(ALU_Ctl1_0), .FlagW1_0(FlagW1_0), .Funct4_1(Funct[4:1]), .Funct0(Funct[0]),
    .ALU_Op(main_decoder_1_alu_op), .NoWrite(NoWrite), .Mov(Mov));
endmodule

module Main_Decoder (
  input  Op1,
  input  Op0,
  input  F5,
  input  F0,
  input  F4,
  output BL,
  output Branch,
  output Mem2Reg,
  output MemWrite,
  output ALUSrc,
  output ImmSrc1,
  output ImmSrc0,
  output RegWrite,
  output RegSrc1,
  output RegSrc0,
  output ALU_op
);

  wire and_1_out, and_2_out, and_3_out, and_4_out, and_5_out;

  and and_1 (and_1_out, ~Op1, ~Op0, ~F5);  // AND_Gate
  and and_2 (and_2_out, ~Op1, ~Op0, F5);  // AND_Gate
  and and_3 (and_3_out, ~Op1, Op0, ~F0);  // AND_Gate
  and and_4 (and_4_out, ~Op1, Op0, F0);  // AND_Gate
  and and_5 (and_5_out, Op1, ~Op0);  // AND_Gate
  and and_6 (BL, and_5_out, F4);
  or or_1 (Branch, 1'b0, and_5_out);
  or or_2 (Mem2Reg, 1'b0, and_4_out);
  or or_3 (MemWrite, 1'b0, and_3_out);
  or or_4 (ALUSrc, 1'b0, and_3_out, and_5_out, and_4_out, and_2_out);
  or or_5 (ImmSrc1, 1'b0, and_5_out);
  or or_6 (ImmSrc0, 1'b0, and_4_out, and_3_out);
  or or_7 (RegWrite, 1'b0, and_2_out, and_4_out, and_1_out);
  or or_8 (RegSrc1, 1'b0, and_3_out);
  or or_9 (RegSrc0, 1'b0, and_5_out);
  or or_10 (ALU_op, and_2_out, and_1_out);
endmodule

module ALU_Decoder (
  input  [3:0] Funct4_1,
  input  ALU_Op,
  input  Funct0,
  output [1:0] ALU_Ctl,
  output [1:0] FlagW1_0,
  output NoWrite,
  output Mov
);

  wire and_1_out, and_2_out, and_3_out, and_4_out, and_5_out, and_7_out, and_8_out, and_9_out, and_10_out,
       or_1_out, or_2_out;

  and and_1 (and_1_out, ~Funct4_1[0], ~Funct4_1[1], Funct4_1[2], ~Funct4_1[3]);  // AND_Gate
  and and_2 (and_2_out, ~Funct4_1[0], Funct4_1[1], ~Funct4_1[2], ~Funct4_1[3]);  // AND_Gate
  and and_3 (and_3_out, ~Funct4_1[0], ~Funct4_1[1], ~Funct4_1[2], ~Funct4_1[3]);  // AND_Gate
  and and_4 (and_4_out, ~Funct4_1[0], ~Funct4_1[1], Funct4_1[2], Funct4_1[3]);  // AND_Gate
  and and_5 (and_5_out, ~Funct4_1[0], Funct4_1[1], ~Funct4_1[2], Funct4_1[3]);  // AND_Gate
  and and_6 (Mov, Funct4_1[0], ~Funct4_1[1], Funct4_1[2], Funct4_1[3]);  // AND_Gate
  and and_7 (and_7_out, and_1_out, Funct0);
  and and_8 (and_8_out, and_2_out, Funct0);
  and and_9 (and_9_out, and_3_out, Funct0);
  and and_10 (and_10_out, and_4_out, Funct0);
  and and_11 (NoWrite, and_5_out, Funct0);
  or or_1 (or_1_out, and_2_out, NoWrite, and_4_out);
  or or_2 (or_2_out, and_4_out, and_3_out);
  or or_3 (FlagW1_0[0], NoWrite, and_8_out, and_7_out);
  or or_4 (FlagW1_0[1], NoWrite, and_8_out, and_10_out, and_9_out, and_7_out);
  and and_12 (ALU_Ctl[0], ALU_Op, or_1_out);
  and and_13 (ALU_Ctl[1], ALU_Op, or_2_out);
endmodule

module PC_Logic (
  input  RegW,
  input  Branch,
  input  [3:0] Rd,
  output PCS
);

  wire and_1_out, comparator_1_eq;

  Comparator #(.width(4)) comparator_1 (.a(Rd), .b(4'b1111), .eq(comparator_1_eq));  // open: gt, lt
  and and_1 (and_1_out, comparator_1_eq, RegW);
  or or_1 (PCS, Branch, and_1_out);
endmodule

module Conditional_Logic (
  input  PCS,
  input  RegW,
  input  NoWrite,
  input  MemW,
  input  [1:0] FlagW,
  input  [3:0] Cond3_0,
  input  CLK,
  input  [3:0] ALUFlags3_0,
  input  CLR,
  output PCSrc,
  output RegWrite,
  output MemWrite
);

  wire [1:0] and_1_out, register_1_q, register_2_q;
  wire [1:1] conditional_execution_1_condex;

  Register #(.width(2)) register_1 (.D(ALUFlags3_0[3:2]), .en(and_1_out[1]), .Q(register_1_q), .clk(CLK), .clr(CLR));
  Register #(.width(2)) register_2 (.D(ALUFlags3_0[1:0]), .en(and_1_out[0]), .Q(register_2_q), .clk(CLK), .clr(CLR));
  assign and_1_out = FlagW & {2{conditional_execution_1_condex[1]}};  // AND_Gate and_1, 2 bits wide
  Conditional_Execution conditional_execution_1 (
    .CondEx(conditional_execution_1_condex[1]), .Cond3_0(Cond3_0), .NZ(register_1_q), .CV(register_2_q));
  and and_2 (PCSrc, PCS, conditional_execution_1_condex[1]);
  and and_3 (RegWrite, RegW, ~NoWrite, conditional_execution_1_condex[1]);  // AND_Gate
  and and_4 (MemWrite, MemW, conditional_execution_1_condex[1]);
endmodule

module Conditional_Execution (
  input  [3:0] Cond3_0,
  input  [1:0] NZ,
  input  [1:0] CV,
  output CondEx
);

  wire and_1_out, and_2_out, and_3_out, and_4_out, and_5_out, and_6_out, not_1_out, not_2_out, xor_1_out,
       xor_2_out;

  not not_1 (not_1_out, NZ[0]);
  and and_1 (and_1_out, ~Cond3_0[3], ~Cond3_0[2], ~Cond3_0[1], ~Cond3_0[0], NZ[0]);  // AND_Gate
  and and_2 (and_2_out, Cond3_0[3], Cond3_0[2], Cond3_0[1], ~Cond3_0[0]);  // AND_Gate
  and and_3 (and_3_out, ~Cond3_0[3], ~Cond3_0[2], ~Cond3_0[1], Cond3_0[0], ~NZ[0]);  // AND_Gate
  xor xor_1 (xor_1_out, NZ[1], CV[0]);
  xor xor_2 (xor_2_out, NZ[1], CV[0]);
  and and_4 (and_4_out, Cond3_0[3], ~Cond3_0[2], Cond3_0[1], Cond3_0[0], xor_1_out);  // AND_Gate
  and and_5 (and_5_out, not_1_out, not_2_out);
  not not_2 (not_2_out, xor_2_out);
  and and_6 (and_6_out, Cond3_0[3], Cond3_0[2], ~Cond3_0[1], ~Cond3_0[0], and_5_out);  // AND_Gate
  or or_1 (CondEx, and_1_out, and_2_out, and_3_out, and_4_out, and_6_out);
endmodule

module Instruction_Memory (
  input  [1:0] Program_Number,
  input  [7:0] A,
  output [31:0] IW
);

  wire [7:0] shifter_1_out;
  wire [31:0] rom_1_data, rom_2_data, rom_3_data, rom_4_data;

  Shifter #(.shift("lr")) shifter_1 (.in(A), .\dist (3'b010), .out(shifter_1_out));
  ROM #(.dataWidth(32)) rom_1 (.addr(shifter_1_out), .data(rom_1_data));  // open: sel
  ROM #(.dataWidth(32)) rom_2 (.addr(shifter_1_out), .data(rom_2_data));  // open: sel
  ROM #(.dataWidth(32)) rom_3 (.addr(shifter_1_out), .data(rom_3_data));  // open: sel
  ROM #(.dataWidth(32)) rom_4 (.addr(shifter_1_out), .data(rom_4_data));  // open: sel
  Multiplexer #(.select(2), .width(32), .enable("false")) multiplexer_1 (
    .in0(rom_1_data), .in1(rom_2_data), .in2(rom_3_data), .in3(rom_4_data), .out(IW), .sel(Program_Number));

  // Notes on the sheet:
  //   contents of rom_1 (hex, n*v repeats v):
  //   4*e28dd0ff e28dd004 e24dd010 e3a00063 e58d000c e3a00048 e58d0008 e3a00028 e58d0004 e3a00000 e58d0000
  //   e1a0000d e3a01004 eaffffff e1a02000 e3a00000 e3a03000 e1530001 a000004 e592c004 e2822004 e080000c
  //   e2833001 eafffff8 eafffffe
  //   contents of rom_2 (hex, n*v repeats v):
  //   4*e28dd0ff e28dd004 e24dd010 e3a00004 e58d000c e3a00001 e58d0008 e3a00009 e58d0004 e3a00003 e58d0000
  //   e1a0000d e3a01004 eaffffff e1a02000 e3a03000 e5920000 e1530001 a000005 e592c000 e2822004 e15c0000
  //   c1a0000c e2833001 eafffff7 eafffffe
  //   contents of rom_3 (hex, n*v repeats v):
  //   e3a00008 e1a01000 e3510002 b1a00001 a000009 e3a0c002 e3a02001 e3a03000 e15c0001 ca000004 e0820003
  //   e1a03002 e1a02000 e28cc001 eafffff8 eafffffe
  //   contents of rom_4 (hex, n*v repeats v):
  //   4*e28dd0ff e28dd004 e3a0000a eb000000 ea000014 e3500002 b12fff1e e24dd00c e58d4000 e58d5004 e58de008
  //   e1a04000 e3a00000 e3a05000 e2440001 ebfffff4 e0855000 e2440002 ebfffff1 e0855000 e1a00005 e59de008
  //   e59d5004 e59d4000 e28dd00c e12fff1e eafffffe
endmodule

module is_branch_exchange (
  input  [31:0] IW,
  output BX
);

  Comparator #(.width(24)) comparator_1 (.a(IW[27:4]), .b(24'h12fff1), .eq(BX));  // open: gt, lt
endmodule
